# Fritzing sketch Project Sketch (saved by Fritzing 0.9.6b)
breadboards: 2

parts:
  S1 = Pushbutton [package="[THT]"]
  ATMEGA328P = Arduino Uno (Rev3)
  R1 = Resistor [tolerance=±5% power=0.25 resistance=220 package=THT]
  S2 = Pushbutton [package="[THT]"]
  R2 = Resistor [tolerance=±5% power=0.25 resistance=220 package=THT]
  LED1 = LED - 5mm [color="Red (633nm)" current=0.030 package="5 mm [THT]"]
  LED2 = LED - 5mm [color="Red (633nm)" current=0.030 package="5 mm [THT]"]
  Step_Motor = Stepper Motor - Bipolar
  Light_Sensor = BH1750

nets:
  5V: S1.Pin_1, S1.Pin_2, ATMEGA328P.5V, R1.Pin_1, S2.Pin_1, S2.Pin_2, R2.Pin_1, Light_Sensor.VCC
  N1: S1.Pin_3, ATMEGA328P.D13/SCK
  N2: ATMEGA328P.A0, LED1.anode
  N3: ATMEGA328P.A1, LED2.anode
  N4: ATMEGA328P.A4/SDA, Light_Sensor.SDA
  N5: ATMEGA328P.A5/SCL, Light_Sensor.SCL
  N6: ATMEGA328P.D8, S2.Pin_3, S2.Pin_4
  N7: ATMEGA328P.D11_PWM/MOSI, Step_Motor.D
  GND: ATMEGA328P.GND, R1.Pin_0, R2.Pin_0, LED1.cathode, LED2.cathode, Light_Sensor.GND
  N8: ATMEGA328P.D3_PWM, Step_Motor.A
  N9: ATMEGA328P.D5_PWM, Step_Motor.B
  N10: ATMEGA328P.D6_PWM, Step_Motor.C

custom parts:
  BH1750: Light Sensor
